// Logisim project item_a.circ as structural Verilog
module item_a (
  input  A,
  input  B,
  input  C,
  output S
);

  wire and_1_out, not_1_out;

  not not_1 (not_1_out, A);
  and and_1 (and_1_out, not_1_out, B);
  or or_1 (S, and_1_out, C);

  // Notes on the sheet:
  //    x = ~AB + C
  //   ver tabela:
  //   projeto > analisar circuito
endmodule
