// Logisim project item_b.circ as structural Verilog
module item_b_2 (
  input  A,
  input  B,
  input  C,
  input  D,
  output S
);

  wire and_1_out, and_2_out, nand_1_out, not_1_out, not_2_out, not_3_out, not_4_out;

  nand nand_1 (nand_1_out, A, B, C);
  and and_1 (and_1_out, A, not_1_out, not_2_out);
  not not_1 (not_1_out, B);
  not not_2 (not_2_out, C);
  not not_3 (not_3_out, A);
  not not_4 (not_4_out, B);
  and and_2 (and_2_out, not_3_out, not_4_out, D);
  or or_1 (S, nand_1_out, and_1_out, and_2_out);
endmodule
